// Logisim project XX.circ as structural Verilog: 1 circuit, main circuit main
module main (
  input  a,
  input  b,
  input  c,
  input  d,
  input  e,
  input  f,
  output y,
  output z,
  output u,
  output out_10
);

  wire nand_1_out, nand_2_out, nand_3_out, nand_4_out, nand_5_out, nand_6_out, nand_7_out, nand_8_out,
       nand_9_out, nand_10_out, nand_11_out, nand_12_out, nand_13_out, nand_14_out, nand_15_out, nand_16_out,
       nand_17_out, nand_18_out, nand_19_out, nand_20_out, nand_21_out, nand_22_out, nand_23_out,
       nand_24_out, nand_25_out, nand_26_out, nand_27_out, nand_28_out, nand_29_out, nand_30_out,
       nand_31_out, nand_32_out, nand_33_out, nand_34_out, nand_35_out, nand_36_out, nand_37_out,
       nand_38_out, nand_39_out, nand_40_out, nand_41_out, nand_42_out, nand_43_out, nand_44_out,
       nand_45_out, nand_46_out, nand_47_out, nand_48_out, nand_49_out, nand_50_out, nand_51_out,
       nand_52_out, nand_53_out, nand_54_out, nand_55_out, nand_56_out, nand_57_out, nand_58_out,
       nand_59_out, nand_60_out, nand_61_out, nand_62_out, nand_63_out, nand_64_out, nand_65_out,
       nand_66_out, nand_67_out, nand_68_out, nand_69_out, nand_70_out, nand_71_out, nand_72_out,
       nand_73_out, nand_74_out, nand_75_out, nand_76_out, nand_77_out, nand_78_out, nand_79_out;

  nand nand_1 (nand_1_out, a, a);
  nand nand_2 (nand_2_out, b, b);
  nand nand_3 (nand_3_out, a, a);
  nand nand_4 (nand_4_out, b, b);
  nand nand_5 (nand_5_out, a, a);
  nand nand_6 (nand_6_out, b, b);
  nand nand_7 (nand_7_out, a, a);
  nand nand_8 (nand_8_out, e, e);
  nand nand_9 (nand_9_out, f, f);
  nand nand_10 (nand_10_out, d, d);
  nand nand_11 (nand_11_out, f, f);
  nand nand_12 (nand_12_out, b, b);
  nand nand_13 (nand_13_out, e, e);
  nand nand_14 (nand_14_out, f, f);
  nand nand_15 (nand_15_out, a, a);
  nand nand_16 (nand_16_out, b, b);
  nand nand_17 (nand_17_out, c, c);
  nand nand_18 (nand_18_out, a, a);
  nand nand_19 (nand_19_out, b, b);
  nand nand_20 (nand_20_out, e, e);
  nand nand_21 (nand_21_out, f, f);
  nand nand_22 (nand_22_out, a, a);
  nand nand_23 (nand_23_out, d, d);
  nand nand_24 (nand_24_out, e, e);
  nand nand_25 (nand_25_out, a, a);
  nand nand_26 (nand_26_out, c, c);
  nand nand_27 (nand_27_out, e, e);
  nand nand_28 (nand_28_out, f, f);
  nand nand_29 (nand_29_out, a, a);
  nand nand_30 (nand_30_out, d, d);
  nand nand_31 (nand_31_out, e, e);
  nand nand_32 (nand_32_out, a, a);
  nand nand_33 (nand_33_out, a, a);
  nand nand_34 (nand_34_out, d, d);
  nand nand_35 (nand_35_out, b, b);
  nand nand_36 (nand_36_out, c, c);
  nand nand_37 (nand_37_out, e, e);
  nand nand_38 (nand_38_out, f, f);
  nand nand_39 (nand_39_out, c, c);
  nand nand_40 (nand_40_out, d, d);
  nand nand_41 (nand_41_out, e, e);
  nand nand_42 (nand_42_out, b, b);
  nand nand_43 (nand_43_out, c, c);
  nand nand_44 (nand_44_out, b, b);
  nand nand_45 (nand_45_out, c, c);
  nand nand_46 (nand_46_out, e, e);
  nand nand_47 (nand_47_out, f, f);
  nand nand_48 (nand_48_out, b, b);
  nand nand_49 (nand_49_out, e, e);
  nand nand_50 (nand_50_out, d, d);
  nand nand_51 (nand_51_out, e, e);
  nand nand_52 (nand_52_out, nand_1_out, nand_2_out, d, f);
  nand nand_53 (nand_53_out, nand_3_out, c, f);
  nand nand_54 (nand_54_out, nand_4_out, c, d, f);
  nand nand_55 (nand_55_out, a, b, c, d, e);
  nand nand_56 (nand_56_out, nand_5_out, nand_6_out, d, f);
  nand nand_57 (nand_57_out, nand_7_out, c, f);
  nand nand_58 (nand_58_out, b, c, d, nand_8_out, nand_9_out);
  nand nand_59 (nand_59_out, a, c, nand_10_out, nand_11_out);
  nand nand_60 (nand_60_out, a, nand_12_out, c, d);
  nand nand_61 (nand_61_out, a, b, d, nand_13_out, nand_14_out);
  nand nand_62 (nand_62_out, nand_15_out, nand_16_out, nand_17_out, d, f);
  nand nand_63 (nand_63_out, nand_18_out, nand_19_out, c, nand_20_out, nand_21_out);
  nand nand_64 (nand_64_out, nand_22_out, c, nand_23_out, nand_24_out);
  nand nand_65 (nand_65_out, nand_25_out, b, nand_26_out, nand_27_out, nand_28_out);
  nand nand_66 (nand_66_out, nand_29_out, b, nand_30_out, nand_31_out);
  nand nand_67 (nand_67_out, nand_32_out, b, c, f);
  nand nand_68 (nand_68_out, nand_33_out, b, c, e);
  nand nand_69 (nand_69_out, b, c, nand_34_out, e);
  nand nand_70 (nand_70_out, a, nand_35_out, nand_36_out, nand_37_out, nand_38_out);
  nand nand_71 (nand_71_out, a, nand_39_out, nand_40_out, nand_41_out);
  nand nand_72 (nand_72_out, a, nand_42_out, d, e);
  nand nand_73 (nand_73_out, a, nand_43_out, d, e);
  nand nand_74 (nand_74_out, a, nand_44_out, c, d, f);
  nand nand_75 (nand_75_out, a, b, nand_45_out, f);
  nand nand_76 (nand_76_out, a, b, c, d, nand_46_out, nand_47_out);
  nand nand_77 (nand_77_out, nand_48_out, d, nand_49_out);
  nand nand_78 (nand_78_out, b, nand_50_out, nand_51_out);
  nand nand_79 (nand_79_out, b, d, e);
  nand nand_80 (y, nand_52_out, nand_53_out, nand_54_out, nand_55_out);
  nand nand_81 (z, nand_56_out, nand_57_out, nand_58_out, nand_59_out, nand_60_out, nand_61_out);
  nand nand_82 (out_10, nand_77_out, nand_78_out, nand_79_out);
  nand nand_83 (u, nand_62_out, nand_63_out, nand_64_out, nand_65_out, nand_66_out, nand_67_out, nand_68_out, nand_69_out, nand_70_out, nand_71_out, nand_72_out, nand_73_out, nand_74_out, nand_75_out, nand_76_out);

  // Notes on the sheet:
  //   Here if 
  //   e      f
  //   0
  //   0
  //   1
  //   0
  //   0
  //   1
  //   Addition
  //   subtraction
  //   multiplication
  //   x
endmodule
